// Logisim project 10.circ as structural Verilog: 1 circuit, main circuit main
module main (
  input  [1:0] in_1,
  output out_2,
  output out_3,
  output out_4,
  output out_5,
  output out_6,
  output out_7
);

  Decoder #(.select(2)) decoder_1 (.out0(out_2), .out1(out_3), .out2(out_4), .out3(out_5), .sel(in_1));  // open: en
  or or_1 (out_6, out_2, out_4, out_5);
  or or_2 (out_7, out_3, out_4);

  // Notes on the sheet:
  //   Name: Ashwin Maharjan
  //   Roll No.: 5
  //   Question No.: 10
endmodule
