// Logisim project 11.circ as structural Verilog: 1 circuit, main circuit main
module main (
  input  A,
  input  B,
  input  C,
  output out_4,
  output out_5,
  output out_6,
  output out_7,
  output out_8,
  output out_9,
  output out_10,
  output out_11
);

  wire not_1_out, not_2_out, not_3_out;

  not not_1 (not_1_out, A);
  not not_2 (not_2_out, B);
  not not_3 (not_3_out, C);
  and and_1 (out_6, C, B);
  and and_2 (out_7, A, B);
  and and_3 (out_8, A, C);
  and and_4 (out_9, not_2_out, not_3_out);
  and and_5 (out_10, not_1_out, not_3_out);
  and and_6 (out_11, A, B, C);
  or or_1 (out_4, out_6, out_7, out_8);
  or or_2 (out_5, out_9, out_10, out_11);

  // Notes on the sheet:
  //   PLA
  //   Name: Ashwin Maharjan
  //   Roll No.: 5
  //   Question No.: 11
endmodule
