// Logisim project 1bi.circ as structural Verilog: 1 circuit, main circuit main
module main (
  input  in_1,
  input  in_2,
  input  in_3,
  input  in_4,
  input  in_5,
  output out_6,
  output out_7,
  output out_8
);

  wire nand_1_out, nand_2_out, nand_3_out;

  nand nand_1 (nand_1_out, in_2, in_3);
  nand nand_2 (nand_2_out, in_4, in_4);
  nand nand_3 (nand_3_out, in_5, in_5);
  nand nand_4 (out_6, in_1, in_1);
  nand nand_5 (out_7, nand_1_out, nand_1_out);
  nand nand_6 (out_8, nand_2_out, nand_3_out);

  // Notes on the sheet:
  //   NAND as NOT
  //   NAND as AND
  //   NAND as OR
  //   Roll No.: 5
  //   Name: Ashwin Maharjan
  //   Question No.: 1 (b)
endmodule
