// Logisim project 1bii.circ as structural Verilog: 1 circuit, main circuit main
module main (
  input  in_1,
  input  in_2,
  input  in_3,
  input  in_4,
  input  in_5,
  output out_6,
  output out_7,
  output out_8
);

  wire nor_2_out, nor_3_out, nor_4_out;

  nor nor_1 (out_6, in_1, in_1);
  nor nor_2 (nor_2_out, in_2, in_2);
  nor nor_3 (nor_3_out, in_3, in_3);
  nor nor_4 (nor_4_out, in_4, in_5);
  nor nor_5 (out_8, nor_4_out, nor_4_out);
  nor nor_6 (out_7, nor_2_out, nor_3_out);

  // Notes on the sheet:
  //   NOR as NOT
  //   NOR as AND
  //   NOR as OR
  //   Name: Ashwin Maharjan
  //   Roll No.: 5
  //   Question No.: 1 (b)
endmodule
