// Logisim project 1d.circ as structural Verilog: 1 circuit, main circuit main
module main (
  input  X,
  input  Y,
  input  X_2,
  input  Z,
  input  Y_2,
  input  Z_2,
  input  X_3,
  input  Y_3,
  input  Z_3,
  input  X_4,
  input  Y_4,
  output out_12
);

  wire nand_1_out, nand_2_out, nand_3_out, nand_4_out, nand_5_out, nand_6_out, nand_7_out, nand_8_out,
       nand_9_out, nand_10_out, nand_11_out, nand_12_out, nor_1_out;

  not nand_1 (nand_1_out, Y);  // NAND_Gate
  not nand_2 (nand_2_out, Z);  // NAND_Gate
  not nand_3 (nand_3_out, Y_2);  // NAND_Gate
  not nand_4 (nand_4_out, Z_2);  // NAND_Gate
  not nand_5 (nand_5_out, Y_3);  // NAND_Gate
  not nand_6 (nand_6_out, Z_3);  // NAND_Gate
  not nand_7 (nand_7_out, X_4);  // NAND_Gate
  nand nand_8 (nand_8_out, X, nand_1_out);
  nand nand_9 (nand_9_out, X_2, nand_2_out);
  nand nand_10 (nand_10_out, nand_3_out, nand_4_out);
  nand nand_11 (nand_11_out, X_3, nand_5_out, nand_6_out);
  nand nand_12 (nand_12_out, nand_7_out, Y_4);
  nor nor_1 (nor_1_out, nand_8_out, nand_9_out, nand_10_out, nand_11_out, nand_12_out);
  not nor_2 (out_12, nor_1_out);  // NOR_Gate

  // Notes on the sheet:
  //   Roll No.: 5
  //   Name: Ashwin Maharjan
  //   Question No.: 1 (d)
endmodule
