// Logisim project 1e.circ as structural Verilog: 1 circuit, main circuit main
module main (
  input  in_1,
  input  in_2,
  input  in_3,
  input  in_4,
  input  in_5,
  input  in_6,
  input  in_7,
  input  in_8,
  output out_9,
  output out_10,
  output out_11,
  output out_12
);

  wire and_1_out, not_1_out, not_2_out, not_4_out, not_5_out, or_2_out;

  and and_1 (and_1_out, in_1, in_3);
  not not_1 (not_1_out, in_5);
  not not_2 (not_2_out, in_7);
  not not_3 (out_9, and_1_out);
  or or_1 (out_11, not_1_out, not_2_out);
  or or_2 (or_2_out, in_2, in_4);
  not not_4 (not_4_out, in_6);
  not not_5 (not_5_out, in_8);
  not not_6 (out_10, or_2_out);
  and and_2 (out_12, not_4_out, not_5_out);

  // Notes on the sheet:
  //   is equivalent to
  //   Roll No.: 5
  //   De-Morgan's Law
  //   Name: Ashwin Maharjan
  //   Question No.: 1 (e)
  //   is equivalent to
endmodule
