// Logisim project 1f.circ as structural Verilog: 1 circuit, main circuit main
module main (
  input  in_1,
  input  in_2,
  input  in_3,
  input  in_4,
  input  in_5,
  input  in_6,
  input  in_7,
  input  in_8,
  input  in_9,
  input  in_10,
  input  in_11,
  input  in_12,
  input  in_13,
  input  in_14,
  output out_15,
  output out_16,
  output out_17,
  output out_18
);

  wire and_1_out, and_2_out, and_4_out, or_1_out, or_3_out, or_4_out;

  or or_1 (or_1_out, in_1, in_3);
  and and_1 (and_1_out, in_7, in_9);
  and and_2 (and_2_out, in_11, in_13);
  and and_3 (out_16, or_1_out, in_6);
  or or_2 (out_17, and_1_out, and_2_out);
  and and_4 (and_4_out, in_2, in_4);
  or or_3 (or_3_out, in_8, in_10);
  or or_4 (or_4_out, in_12, in_14);
  or or_5 (out_15, and_4_out, in_5);
  and and_5 (out_18, or_3_out, or_4_out);

  // Notes on the sheet:
  //   is equivalent to
  //   Roll No.: 5
  //   Name: Ashwin Maharjan
  //   Question No.: 1 (f)
  //   Distributive Law
  //   is equivalent to
endmodule
