// Logisim project 2a.circ as structural Verilog: 1 circuit, main circuit main
module main (
  input  A,
  input  B,
  input  C,
  input  D,
  input  A_2,
  input  B_2,
  input  C_2,
  input  D_2,
  output out_9
);

  wire nor_1_out, nor_2_out, nor_3_out, nor_4_out, nor_5_out, nor_6_out, nor_7_out, nor_8_out, nor_9_out;

  nor nor_1 (nor_1_out, A, A);
  nor nor_2 (nor_2_out, B, B);
  nor nor_3 (nor_3_out, C, C);
  nor nor_4 (nor_4_out, D, D);
  not nor_5 (nor_5_out, nor_2_out);  // NOR_Gate
  nor nor_6 (nor_6_out, B, nor_3_out, nor_4_out);
  nor nor_7 (nor_7_out, A_2, B_2, C_2, D_2);
  nor nor_8 (nor_8_out, nor_1_out, B, nor_4_out);
  nor nor_9 (nor_9_out, nor_5_out, nor_8_out, nor_6_out, nor_7_out);
  nor nor_10 (out_9, nor_9_out, nor_9_out);

  // Notes on the sheet:
  //   Roll No.: 5
  //   Name: Ashwin Maharjan
  //   Question No.: 2 (a)
endmodule
