// Logisim project 2b.circ as structural Verilog: 1 circuit, main circuit main
module main (
  input  C,
  input  D,
  input  A,
  input  B,
  input  C_2,
  input  D_2,
  output out_7
);

  wire nand_1_out, nand_2_out, nand_3_out, nand_4_out, nand_5_out, nand_6_out;

  not nand_1 (nand_1_out, D);  // NAND_Gate
  not nand_2 (nand_2_out, C_2);  // NAND_Gate
  nand nand_3 (nand_3_out, C, nand_1_out);
  nand nand_4 (nand_4_out, A, C);
  nand nand_5 (nand_5_out, A, D);
  nand nand_6 (nand_6_out, B, nand_2_out, D_2);
  nand nand_7 (out_7, nand_3_out, nand_4_out, nand_5_out, nand_6_out);

  // Notes on the sheet:
  //   Roll No.: 5
  //   Question No.: 2 (b)
  //   Name: Ashwin Maharjan
endmodule
