// Logisim project 3c.circ as structural Verilog: 1 circuit, main circuit main
module main (
  input  in_1,
  input  in_2,
  input  in_3,
  input  in_4,
  input  in_5,
  output out_6,
  output out_7,
  output out_8,
  output out_9
);

  wire and_2_out, and_3_out, not_1_out, not_2_out, not_3_out, xor_2_out;

  xor xor_1 (out_6, in_1, in_2);
  not not_1 (not_1_out, in_1);
  xor xor_2 (xor_2_out, in_3, in_4);
  and and_1 (out_7, not_1_out, in_2);
  not not_2 (not_2_out, xor_2_out);
  not not_3 (not_3_out, in_3);
  xor xor_3 (out_8, xor_2_out, in_5);
  and and_2 (and_2_out, in_5, not_2_out);
  and and_3 (and_3_out, not_3_out, in_4);
  or or_1 (out_9, and_2_out, and_3_out);

  // Notes on the sheet:
  //   Half Subtractor
  //   Full Subtractor
  //   Name: Ashwin Maharjan
  //   Roll No.: 5
  //   Question No.: 3 (c)
endmodule
