// Logisim project 3e.circ as structural Verilog: 1 circuit, main circuit main
module main (
  input  A,
  input  B,
  input  C,
  input  in_4,
  output Y1,
  output Y2,
  output Y3,
  output Y4,
  output Y5,
  output Y6
);

  wire and_2_out, and_3_out, not_1_out, not_2_out, xor_1_out;

  not not_1 (not_1_out, B);
  not not_2 (not_2_out, C);
  and and_1 (Y1, A, B);
  and and_2 (and_2_out, A, not_1_out);
  and and_3 (and_3_out, A, C);
  xor xor_1 (xor_1_out, A, B);
  and and_4 (Y4, B, not_2_out);
  and and_5 (Y3, xor_1_out, C);
  or or_1 (Y2, and_2_out, and_3_out);

  assign Y5 = in_4;
  assign Y6 = C;

  // Notes on the sheet:
  //   Roll No.: 5
  //   Name: Ashwin Maharjan
  //   Question No.: 3 (e)
endmodule
