// Logisim project 3f.circ as structural Verilog: 1 circuit, main circuit Question No.: 3 (f)
module Question_No___3__f (
  input  A,
  input  B,
  input  C,
  input  D,
  output Y1,
  output Y2,
  output Y3,
  output Y4
);

  xor xor_1 (Y2, A, B);
  xor xor_2 (Y3, B, C);
  xor xor_3 (Y4, C, D);

  assign Y1 = A;

  // Notes on the sheet:
  //   Roll No.: 5
  //   Question No.: 3 (f)
  //   Name: Ashwin Maharjan
endmodule
