// Logisim project 3g(i).circ as structural Verilog: 1 circuit, main circuit main
module main (
  input  A,
  input  B,
  input  C,
  input  D,
  output out_5,
  output out_6,
  output out_7,
  output out_8
);

  wire and_1_out, and_2_out, and_3_out, and_4_out, and_5_out, not_1_out, not_2_out, not_3_out;

  and and_1 (and_1_out, B, D);
  and and_2 (and_2_out, B, C);
  not not_1 (not_1_out, B);
  not not_2 (not_2_out, C);
  not not_3 (not_3_out, D);
  not not_4 (out_8, D);
  and and_3 (and_3_out, not_1_out, D);
  and and_4 (and_4_out, B, C);
  and and_5 (and_5_out, B, not_2_out, not_3_out);
  xnor xnor_1 (out_7, C, D);
  or or_1 (out_5, A, and_1_out, and_2_out);
  or or_2 (out_6, and_3_out, and_4_out, and_5_out);

  // Notes on the sheet:
  //   Roll No.: 5
  //   Name: Ashwin Maharjan
  //   Question No.: 3 (g) (i)
endmodule
