// Logisim project 3g(ii).circ as structural Verilog: 1 circuit, main circuit main
module main (
  input  A,
  input  B,
  input  C,
  input  D,
  input  A_2,
  input  B_2,
  input  C_2,
  input  D_2,
  output out_9,
  output out_10
);

  wire xor_1_out, xor_2_out, xor_3_out, xor_4_out;

  xor xor_1 (xor_1_out, A, B);
  xor xor_2 (xor_2_out, A_2, B_2);
  xor xor_3 (xor_3_out, xor_1_out, C);
  xor xor_4 (xor_4_out, xor_2_out, C_2);
  xor xor_5 (out_9, xor_3_out, D);
  xnor xnor_1 (out_10, xor_4_out, D_2);

  // Notes on the sheet:
  //   Name: Ashwin Maharjan
  //   Roll No.: 5
  //   Question No.: 3 (g) (ii)
endmodule
