// Logisim project 4a.circ as structural Verilog: 1 circuit, main circuit main
module main (
  input  S,
  input  in_2,
  input  in_3,
  output out_4
);

  wire and_1_out, and_2_out, not_1_out;

  not not_1 (not_1_out, S);
  and and_1 (and_1_out, not_1_out, in_2);
  and and_2 (and_2_out, S, in_3);
  or or_1 (out_4, and_1_out, and_2_out);

  // Notes on the sheet:
  //   Roll No.: 5
  //   Question No.: 4 (a)
  //   Name: Ashwin Maharjan
endmodule
