// Logisim project 4b(i).circ as structural Verilog: 1 circuit, main circuit main
module main (
  input  S1,
  input  S2,
  input  in_3,
  input  in_4,
  input  in_5,
  input  in_6,
  input  in_7,
  input  [1:0] in_8,
  input  in_9,
  input  in_10,
  input  in_11,
  output out_12,
  output out_13
);

  wire and_1_out, and_2_out, and_3_out, and_4_out, not_1_out, not_2_out;

  Multiplexer #(.select(2)) multiplexer_1 (
    .in0(in_3), .in1(in_4), .in2(in_5), .in3(in_6), .out(out_12), .sel(in_8));  // open: en
  not not_1 (not_1_out, S1);
  not not_2 (not_2_out, S2);
  and and_1 (and_1_out, not_1_out, not_2_out, in_7);
  and and_2 (and_2_out, not_1_out, S2, in_9);
  and and_3 (and_3_out, S1, not_2_out, in_10);
  and and_4 (and_4_out, S1, S2, in_11);
  or or_1 (out_13, and_1_out, and_2_out, and_3_out, and_4_out);

  // Notes on the sheet:
  //   Name: Ashwin Maharjan
  //   Roll No.: 5
  //   Question No.: 4 (b) (i)
endmodule
