// Logisim project 4b(ii).circ as structural Verilog: 1 circuit, main circuit main
module main (
  input  in_1,
  input  in_2,
  input  in_3,
  input  S2,
  input  S1,
  input  S2_2,
  input  in_7,
  input  in_8,
  input  in_9,
  input  in_10,
  input  in_11,
  input  in_12,
  input  [2:0] in_13,
  input  in_14,
  input  in_15,
  input  in_16,
  input  in_17,
  input  in_18,
  input  in_19,
  input  in_20,
  output out_21,
  output out_22
);

  wire and_1_out, and_2_out, and_3_out, and_4_out, and_5_out, and_6_out, and_7_out, and_8_out, not_1_out,
       not_2_out, not_3_out;

  not not_1 (not_1_out, S2);
  not not_2 (not_2_out, S1);
  not not_3 (not_3_out, S2_2);
  and and_1 (and_1_out, not_1_out, not_2_out, not_3_out, in_12);
  and and_2 (and_2_out, not_1_out, not_2_out, S2_2, in_14);
  and and_3 (and_3_out, not_1_out, S1, not_3_out, in_15);
  and and_4 (and_4_out, not_1_out, S1, S2_2, in_16);
  and and_5 (and_5_out, S2, not_2_out, not_3_out, in_17);
  and and_6 (and_6_out, not_2_out, S2_2, in_18);
  and and_7 (and_7_out, S2, S1, not_3_out, in_19);
  and and_8 (and_8_out, S2, S1, S2_2, in_20);
  or or_1 (out_22, and_1_out, and_2_out, and_3_out, and_4_out, and_5_out, and_6_out, and_7_out, and_8_out);
  Multiplexer #(.select(3)) multiplexer_1 (
    .in0(in_1), .in1(in_2), .in2(in_3), .in3(in_7), .in4(in_8), .in5(in_9), .in6(in_10), .in7(in_11),
    .out(out_21), .sel(in_13));  // open: en

  // Notes on the sheet:
  //   Roll No.: 5
  //   Name: Ashwin Maharjan
  //   Question No.: 4 (b) (ii)
endmodule
