// Logisim project 4c.circ as structural Verilog: 1 circuit, main circuit main
module main (
  input  in_1,
  input  in_2,
  input  in_3,
  input  in_4,
  input  [1:0] in_5,
  input  in_6,
  input  in_7,
  input  in_8,
  input  in_9,
  input  in_10,
  input  [1:0] in_11,
  output I6
);

  wire multiplexer_1_out, multiplexer_2_out, not_1_out;

  not not_1 (not_1_out, in_6);
  Multiplexer #(.select(2)) multiplexer_1 (
    .in0(in_1), .in1(in_2), .in2(in_3), .in3(in_4), .out(multiplexer_1_out), .sel(in_5), .en(not_1_out));
  Multiplexer #(.select(2)) multiplexer_2 (
    .in0(in_7), .in1(in_8), .in2(in_9), .in3(in_10), .out(multiplexer_2_out), .sel(in_11), .en(in_6));
  or or_1 (I6, multiplexer_1_out, multiplexer_2_out);

  // Notes on the sheet:
  //   Implementation of 8x1 mux using 4x1 mux
  //   Roll No.: 5
  //   Question No.: 4 (c)
  //   Name: Ashwin Maharjan
endmodule
