// Logisim project 4d.circ as structural Verilog: 1 circuit, main circuit main
module main (
  input  A,
  input  _1,
  input  [2:0] in_3,
  output out_4
);

  wire not_1_out, not_2_out;

  not not_1 (not_1_out, A);
  not not_2 (not_2_out, _1);
  Multiplexer #(.select(3)) multiplexer_1 (
    .in0(_1), .in1(not_2_out), .in2(not_1_out), .in3(not_2_out), .in4(not_1_out), .in5(A), .in6(not_1_out),
    .in7(A), .out(out_4), .sel(in_3));  // open: en

  // Notes on the sheet:
  //   Name: Ashwin Maharjan
  //   Roll No.: 5
  //   Question No.: 4 (d)
endmodule
