// Logisim project 4e.circ as structural Verilog: 1 circuit, main circuit main
module main (
  input  D,
  input  S2,
  input  S1,
  input  S0,
  input  in_5,
  input  [2:0] in_6,
  output out_7,
  output out_8,
  output out_9,
  output out_10,
  output out_11,
  output out_12,
  output out_13,
  output out_14,
  output out_15,
  output out_16,
  output out_17,
  output out_18,
  output out_19,
  output out_20,
  output out_21,
  output out_22
);

  wire nor_1_out, nor_2_out, nor_3_out, nor_4_out, nor_5_out, nor_6_out, nor_7_out, nor_8_out, not_1_out,
       not_2_out, not_3_out;

  not not_1 (not_1_out, S1);
  not not_2 (not_2_out, S2);
  not not_3 (not_3_out, S0);
  nor nor_1 (nor_1_out, D, not_2_out, not_1_out, not_3_out);
  nor nor_2 (nor_2_out, D, not_2_out, not_1_out, S0);
  nor nor_3 (nor_3_out, D, not_2_out, S1, not_3_out);
  nor nor_4 (nor_4_out, D, not_2_out, S1, S0);
  nor nor_5 (nor_5_out, D, S2, not_1_out, not_3_out);
  nor nor_6 (nor_6_out, D, S2, not_1_out, S0);
  nor nor_7 (nor_7_out, D, S2, S1, not_3_out);
  nor nor_8 (nor_8_out, D, S2, S1, S0);
  nor nor_9 (out_12, nor_1_out, nor_1_out);
  nor nor_10 (out_16, nor_2_out, nor_2_out);
  nor nor_11 (out_17, nor_3_out, nor_3_out);
  nor nor_12 (out_18, nor_4_out, nor_4_out);
  nor nor_13 (out_19, nor_5_out, nor_5_out);
  nor nor_14 (out_20, nor_6_out, nor_6_out);
  nor nor_15 (out_21, nor_7_out, nor_7_out);
  nor nor_16 (out_22, nor_8_out, nor_8_out);
  Demultiplexer #(.select(3)) demultiplexer_1 (
    .out0(out_7), .out1(out_8), .out2(out_9), .out3(out_10), .out4(out_11), .out5(out_13), .out6(out_14),
    .out7(out_15), .in(in_5), .sel(in_6));  // open: en

  // Notes on the sheet:
  //   Roll No.: 5
  //   Question No.: 4 (e)
  //   Name: Ashwin Maharjan
endmodule
