// Logisim project 5a.circ as structural Verilog: 1 circuit, main circuit main
module main (
  input  D0,
  input  D1,
  input  D2,
  input  D3,
  input  D4,
  input  D5,
  input  D6,
  input  D7,
  output A,
  output B,
  output C
);

  or or_1 (A, D4, D5, D6, D7);
  or or_2 (B, D2, D3, D6, D7);
  or or_3 (C, D1, D3, D5, D7);

  // Notes on the sheet:
  //   Octal to Binary Encoder
  //   Roll No.: 5
  //   Name: Ashwin Maharjan
  //   Question No.: 5 (a)
endmodule
