// Logisim project 5b.circ as structural Verilog: 1 circuit, main circuit main
module main (
  input  D0,
  input  D1,
  input  D2,
  input  D3,
  input  D4,
  input  D5,
  input  D6,
  input  D7,
  input  D8,
  input  D9,
  input  D10,
  input  D11,
  input  D12,
  input  D13,
  input  D14,
  input  D15,
  output out_17,
  output out_18,
  output out_19,
  output out_20
);

  or or_1 (out_17, D8, D9, D10, D12, D13, D14, D15);
  or or_2 (out_18, D4, D5, D6, D12, D13, D14, D15);
  or or_3 (out_19, D2, D3, D6, D12, D13, D14, D15);
  or or_4 (out_20, D1, D3, D5, D9, D11, D13, D15);

  // Notes on the sheet:
  //   Roll No.: 5
  //   Question No.: 5 (b)
  //   Name: Ashwin Maharjan
endmodule
