// Logisim project 5c.circ as structural Verilog: 1 circuit, main circuit main
module main (
  input  A,
  input  B,
  input  C,
  input  [2:0] in_4,
  output out_5,
  output out_6,
  output out_7,
  output out_8,
  output out_9,
  output out_10,
  output out_11,
  output out_12,
  output out_13,
  output out_14,
  output out_15,
  output out_16,
  output out_17,
  output out_18,
  output out_19,
  output out_20
);

  wire not_1_out, not_2_out, not_3_out;

  not not_1 (not_1_out, A);
  not not_2 (not_2_out, C);
  not not_3 (not_3_out, B);
  and and_1 (out_5, not_1_out, not_3_out, not_2_out);
  and and_2 (out_12, not_1_out, not_3_out, C);
  and and_3 (out_15, not_1_out, B, not_2_out);
  and and_4 (out_16, not_1_out, B, C);
  and and_5 (out_17, A, not_3_out, not_2_out);
  and and_6 (out_18, A, not_3_out, C);
  and and_7 (out_19, A, B, not_2_out);
  and and_8 (out_20, A, B, C);
  Decoder #(.select(3)) decoder_1 (
    .out0(out_6), .out1(out_7), .out2(out_8), .out3(out_9), .out4(out_10), .out5(out_11), .out6(out_13),
    .out7(out_14), .sel(in_4));  // open: en

  // Notes on the sheet:
  //   Name: Ashwin Maharjan
  //   Roll No.: 5
  //   Question No.: 5 (c)
endmodule
