// Logisim project 5d.circ as structural Verilog: 1 circuit, main circuit main
module main (
  input  in_1,
  input  [2:0] in_2,
  input  [2:0] in_3,
  output D0,
  output D1,
  output D3,
  output D2,
  output D5,
  output D6,
  output D7,
  output out_11,
  output D8,
  output D9,
  output D11,
  output D10,
  output D13,
  output D14,
  output D15,
  output out_19
);

  wire not_1_out;

  not not_1 (not_1_out, in_1);
  Decoder #(.select(3)) decoder_1 (
    .out0(D0), .out1(D1), .out2(D3), .out3(D2), .out4(D5), .out5(D6), .out6(D7), .out7(out_11), .sel(in_2),
    .en(not_1_out));
  Decoder #(.select(3)) decoder_2 (
    .out0(D8), .out1(D9), .out2(D11), .out3(D10), .out4(D13), .out5(D14), .out6(D15), .out7(out_19),
    .sel(in_3), .en(in_1));

  // Notes on the sheet:
  //   Implementation of 4x16 decoder using 3x8 decoder
  //   D4
  //   D12
  //   Roll No.: 5
  //   Name: Ashwin Maharjan
  //   Question No.: 5 (d)
endmodule
