// Logisim project 6a.circ as structural Verilog: 1 circuit, main circuit main
module main (
  input  A,
  input  B,
  input  C,
  input  D,
  output out_5,
  output out_6,
  output out_7,
  output out_8,
  output out_9,
  output out_10,
  output out_11
);

  wire and_1_out, and_2_out, and_3_out, and_4_out, and_5_out, and_6_out, and_7_out, and_8_out, and_9_out,
       and_10_out, nor_1_out, not_1_out, not_2_out, not_3_out, not_4_out, xnor_1_out, xor_1_out;

  not not_1 (not_1_out, A);
  not not_2 (not_2_out, B);
  not not_3 (not_3_out, D);
  not not_4 (not_4_out, C);
  and and_1 (and_1_out, C, not_3_out);
  and and_2 (and_2_out, not_2_out, not_3_out);
  and and_3 (and_3_out, not_2_out, C);
  and and_4 (and_4_out, B, not_4_out, D);
  nor nor_1 (nor_1_out, B, C);
  not xnor_1 (xnor_1_out, B);  // XNOR_Gate
  buf xor_1 (xor_1_out, C);  // XOR_Gate
  and and_5 (and_5_out, C, not_3_out);
  and and_6 (and_6_out, not_2_out, not_3_out);
  and and_7 (and_7_out, not_4_out, not_3_out);
  and and_8 (and_8_out, B, not_3_out);
  and and_9 (and_9_out, B, not_4_out);
  and and_10 (and_10_out, C, not_3_out);
  or or_1 (out_5, A, C, xnor_1_out);
  or or_2 (out_6, xor_1_out, not_2_out);
  or or_3 (out_7, B, not_4_out, D);
  or or_4 (out_8, and_1_out, and_2_out, and_3_out, and_4_out, A);
  or or_5 (out_9, and_5_out, and_6_out);
  or or_6 (out_11, and_10_out, A, nor_1_out);
  or or_7 (out_10, and_7_out, A, and_8_out, and_9_out);

  // Notes on the sheet:
  //   Roll No.: 5
  //   Question No.: 6 (a)
  //   Name: Ashwin Maharjan
endmodule
