// Logisim project 6c.circ as structural Verilog: 1 circuit, main circuit main
module main (
  input  _1,
  input  B,
  input  D,
  input  C,
  input  _1_2,
  input  C_2,
  input  A,
  input  _1_3,
  output a_2,
  output b_2,
  output c_3,
  output d_2,
  output e,
  output f,
  output g
);

  wire not_1_out, not_2_out, not_4_out;

  not not_1 (not_1_out, B);
  not not_2 (not_2_out, D);
  not not_3 (c_3, C);
  or or_1 (e, C_2, A);
  and and_1 (b_2, not_1_out, not_2_out);
  not not_4 (not_4_out, C_2);
  or or_2 (f, not_4_out, A);

  assign a_2 = _1;
  assign d_2 = _1_2;
  assign g = _1_3;

  // Notes on the sheet:
  //   Roll No.: 5
  //   Question No.: 6 (c)
  //   Name: Ashwin Maharjan
endmodule
