// Logisim project 7b(i).circ as structural Verilog: 1 circuit, main circuit main
module main (
  input  in_1,
  input  in_2,
  output out_3,
  output out_4
);

  wire clock_1_out, nor_1_out, nor_2_out;

  Clock clock_1 (.out(clock_1_out));
  nor nor_1 (nor_1_out, in_1, clock_1_out);
  nor nor_2 (nor_2_out, clock_1_out, in_2);
  nor nor_3 (out_3, nor_1_out, out_4);
  nor nor_4 (out_4, out_3, nor_2_out);

  // Notes on the sheet:
  //   Roll No.: 5
  //   Question No.: 7 (b) (i)
  //   SR Flip Flop
  //   Name: Ashwin Maharjan
endmodule
