// Logisim project 7b(iii).circ as structural Verilog: 1 circuit, main circuit main
module main (
  input  in_1,
  input  in_2,
  output out_3,
  output out_4
);

  wire clock_1_out, nand_1_out, nand_2_out;

  Clock clock_1 (.out(clock_1_out));
  nand nand_1 (nand_1_out, out_4, in_1, clock_1_out);
  nand nand_2 (nand_2_out, clock_1_out, in_2, out_3);
  nor nor_1 (out_3, nand_1_out, out_4);
  nor nor_2 (out_4, out_3, nand_2_out);

  // Notes on the sheet:
  //   Roll No.: 5
  //   JK Flip Flop
  //   Name: Ashwin Maharjan
  //   Question No.: 7 (b) (iii)
endmodule
