// Logisim project 7b(iv).circ as structural Verilog: 1 circuit, main circuit main
module main (
  input  in_1,
  output out_2,
  output out_3
);

  wire clock_1_out, nand_1_out, nand_2_out;

  Clock clock_1 (.out(clock_1_out));
  nand nand_1 (nand_1_out, out_2, in_1, clock_1_out);
  nand nand_2 (nand_2_out, clock_1_out, in_1, out_3);
  nor nor_1 (out_2, nand_1_out, out_3);
  nor nor_2 (out_3, out_2, nand_2_out);

  // Notes on the sheet:
  //   Roll No.: 5
  //   T Flip Flop
  //   Name: Ashwin Maharjan
  //   Question No.: 7 (b) (iv)
endmodule
