// Logisim project 7c.circ as structural Verilog: 1 circuit, main circuit main
module main (
  input  in_1,
  input  in_2,
  output out_3,
  output out_4
);

  wire clock_1_out, nand_1_out, nand_2_out, nand_3_out, nand_4_out, nor_1_out, nor_2_out, not_1_out;

  Clock clock_1 (.out(clock_1_out));
  not not_1 (not_1_out, clock_1_out);
  nand nand_1 (nand_1_out, out_4, in_1, clock_1_out);
  nand nand_2 (nand_2_out, clock_1_out, in_2, out_3);
  nor nor_1 (nor_1_out, nand_1_out, nor_2_out);
  nor nor_2 (nor_2_out, nor_1_out, nand_2_out);
  nand nand_3 (nand_3_out, nor_1_out, not_1_out);
  nand nand_4 (nand_4_out, not_1_out, nor_2_out);
  nor nor_3 (out_3, nand_3_out, out_4);
  nor nor_4 (out_4, out_3, nand_4_out);

  // Notes on the sheet:
  //   Roll No.: 5
  //   Question No.: 7 (c)
  //   Master Slave Flip Flop
  //   Name: Ashwin Maharjan
endmodule
