// Logisim project 8a.circ as structural Verilog: 1 circuit, main circuit main
module main (
  input  in_1,
  input  in_2,
  output out_3,
  output out_4,
  output out_5,
  output out_6
);

  wire and_1_out, and_2_out, and_3_out, and_4_out, and_5_out, and_6_out, clock_1_out, not_1_out, or_1_out,
       or_2_out, or_3_out, t_ff_1_qn, t_ff_2_qn, t_ff_3_qn;

  not not_1 (not_1_out, in_1);
  Clock clock_1 (.out(clock_1_out));
  T_Flip_Flop t_ff_1 (.clk(clock_1_out), .T(in_2), .Q(out_3), .Qn(t_ff_1_qn));  // open: preset, reset, en
  and and_1 (and_1_out, in_1, out_3);
  and and_2 (and_2_out, t_ff_1_qn, not_1_out);
  or or_1 (or_1_out, and_1_out, and_2_out);
  and and_3 (and_3_out, in_1, out_4);
  T_Flip_Flop t_ff_2 (.clk(or_1_out), .T(in_2), .Q(out_4), .Qn(t_ff_2_qn));  // open: preset, reset, en
  and and_4 (and_4_out, t_ff_2_qn, not_1_out);
  or or_2 (or_2_out, and_3_out, and_4_out);
  T_Flip_Flop t_ff_3 (.clk(or_2_out), .T(in_2), .Q(out_5), .Qn(t_ff_3_qn));  // open: preset, reset, en
  and and_5 (and_5_out, in_1, out_5);
  and and_6 (and_6_out, t_ff_3_qn, not_1_out);
  or or_3 (or_3_out, and_5_out, and_6_out);
  T_Flip_Flop t_ff_4 (.clk(or_3_out), .T(in_2), .Q(out_6));  // open: Qn, preset, reset, en

  // Notes on the sheet:
  //   Roll No.: 5
  //   Name: Ashwin Maharjan
  //   Question No.: 8 (a)
  //   4 bit asynchronous up/down counter using T-FF
endmodule
