// Logisim project 8b.circ as structural Verilog: 1 circuit, main circuit main
module main (
  input  _1,
  input  _1_2,
  input  _1_3,
  input  _1_4,
  output out_5,
  output out_6,
  output out_7,
  output out_8
);

  wire clock_1_out, nand_1_out;

  Clock clock_1 (.out(clock_1_out));
  J_K_Flip_Flop j_k_ff_1 (.J(_1), .clk(clock_1_out), .K(_1), .Q(_1_2), .reset(nand_1_out));  // open: Qn, preset, en
  nand nand_1 (nand_1_out, _1_2, out_7, out_8);
  J_K_Flip_Flop j_k_ff_2 (.J(_1_2), .clk(_1_2), .K(_1_2), .Q(out_6), .reset(nand_1_out));  // open: Qn, preset, en
  J_K_Flip_Flop j_k_ff_3 (.J(_1_3), .clk(out_6), .K(_1_3), .Q(out_7), .reset(nand_1_out));  // open: Qn, preset, en
  J_K_Flip_Flop j_k_ff_4 (.J(_1_4), .clk(out_7), .K(_1_4), .Q(out_8), .reset(nand_1_out));  // open: Qn, preset, en

  assign out_5 = _1_2;

  // Notes on the sheet:
  //   MOD 13 asynchronous counter using JK-FF
  //   Name: Ashwin Maharjan
  //   Roll No.: 5
  //   Question No.: 8 (b)
endmodule
