// Logisim project 8c.circ as structural Verilog: 1 circuit, main circuit main
module main (
);

  wire and_1_out, clock_1_out, d_ff_1_q, d_ff_1_qn, d_ff_2_q, d_ff_2_qn, d_ff_3_q, d_ff_3_qn, d_ff_4_q,
       d_ff_4_qn;

  Clock clock_1 (.out(clock_1_out));
  D_Flip_Flop d_ff_1 (
    .clk(clock_1_out), .D(d_ff_1_qn), .Q(d_ff_1_q), .Qn(d_ff_1_qn), .en(and_1_out));  // open: preset, reset
  and and_1 (and_1_out, d_ff_2_q, d_ff_4_q);
  D_Flip_Flop d_ff_2 (
    .clk(d_ff_1_q), .D(d_ff_2_qn), .Q(d_ff_2_q), .Qn(d_ff_2_qn), .en(and_1_out));  // open: preset, reset
  D_Flip_Flop d_ff_3 (
    .clk(d_ff_2_q), .D(d_ff_3_qn), .Q(d_ff_3_q), .Qn(d_ff_3_qn), .en(and_1_out));  // open: preset, reset
  D_Flip_Flop d_ff_4 (
    .clk(d_ff_3_q), .D(d_ff_4_qn), .Q(d_ff_4_q), .Qn(d_ff_4_qn), .en(and_1_out));  // open: preset, reset

  // Notes on the sheet:
  //   Decade asynchronous counter
  //   Name: Ashwin Maharjan
  //   Roll No.: 5
  //   Question No.: 8 (c)
endmodule
