// Logisim project 8d.circ as structural Verilog: 1 circuit, main circuit main
module main (
  output out_1,
  output out_2,
  output out_3,
  output out_4
);

  wire and_1_out, and_2_out, clock_1_out, not_1_out, or_1_out;

  and and_1 (and_1_out, out_2, out_1, out_4);
  or or_1 (or_1_out, out_2, out_3);
  and and_2 (and_2_out, out_1, out_2);
  not not_1 (not_1_out, out_2);
  Clock clock_1 (.out(clock_1_out));
  J_K_Flip_Flop _3 (.J(and_1_out), .clk(clock_1_out), .K(out_1), .Q(out_4));  // open: Qn, preset, en, reset
  J_K_Flip_Flop _2 (.J(and_2_out), .clk(clock_1_out), .K(and_2_out), .Q(out_3));  // open: Qn, preset, en, reset
  J_K_Flip_Flop _1 (.J(out_2), .clk(clock_1_out), .K(or_1_out), .Q(out_1));  // open: Qn, preset, en, reset
  J_K_Flip_Flop _0 (.J(not_1_out), .clk(clock_1_out), .K(out_2), .Q(out_2));  // open: Qn, preset, en, reset

  // Notes on the sheet:
  //   Roll No.: 5
  //   Question No.: 8 (d)
  //   MOD 11 synchronous counter using JK-FF
  //   Name: Ashwin Maharjan
endmodule
