// Logisim project 8e.circ as structural Verilog: 1 circuit, main circuit main
module main (
  input  M,
  input  _1,
  output out_3,
  output out_4,
  output out_5,
  output out_6
);

  wire and_1_out, and_2_out, clock_1_out, not_1_out, not_2_out, not_3_out, or_1_out, xor_1_out;

  not not_1 (not_1_out, M);
  not not_2 (not_2_out, out_3);
  not not_3 (not_3_out, out_4);
  xor xor_1 (xor_1_out, M, out_3);
  and and_1 (and_1_out, not_1_out, out_3, out_4);
  and and_2 (and_2_out, M, not_2_out, not_3_out);
  or or_1 (or_1_out, and_1_out, and_2_out);
  Clock clock_1 (.out(clock_1_out));
  T_Flip_Flop t_ff_1 (.clk(clock_1_out), .T(or_1_out), .Q(out_5));  // open: Qn, preset, reset, en
  T_Flip_Flop t_ff_2 (.clk(clock_1_out), .T(xor_1_out), .Q(out_4));  // open: Qn, preset, reset, en
  T_Flip_Flop t_ff_3 (.clk(clock_1_out), .T(_1), .Q(out_3));  // open: Qn, preset, reset, en

  assign out_6 = M;

  // Notes on the sheet:
  //   Roll No.: 5
  //   Question No.: 8 (e)
  //   3 bit synchronous up/down counter using T-FF
  //   Name: Ashwin Maharjan
endmodule
