// Logisim project 8f.circ as structural Verilog: 1 circuit, main circuit main
module main (
  input  in_1,
  output out_2,
  output out_3,
  output out_4
);

  wire clock_1_out, xor_1_out;

  xor xor_1 (xor_1_out, out_4, out_3);
  Clock clock_1 (.out(clock_1_out));
  D_Flip_Flop d_ff_1 (.clk(clock_1_out), .D(xor_1_out), .Q(out_4));  // open: Qn, preset, en, reset
  D_Flip_Flop d_ff_2 (.clk(clock_1_out), .D(out_3), .Q(out_3));  // open: Qn, preset, en, reset
  D_Flip_Flop d_ff_3 (.clk(clock_1_out), .D(in_1), .Q(out_2));  // open: Qn, preset, en, reset

  // Notes on the sheet:
  //   Roll No.: 5
  //   Synchronous counter from 0-7
  //   Name: Ashwin Maharjan
  //   Question No.: 8 (f)
endmodule
