// Logisim project 8g(i).circ as structural Verilog: 1 circuit, main circuit main
module main (
  input  in_1,
  output out_2
);

  wire and_1_out, clock_1_out, d_ff_1_q, d_ff_2_q, d_ff_3_q;

  Clock clock_1 (.out(clock_1_out));
  D_Flip_Flop d_ff_1 (.clk(clock_1_out), .D(in_1), .Q(d_ff_1_q), .en(and_1_out));  // open: Qn, preset, reset
  and and_1 (and_1_out, d_ff_1_q, d_ff_2_q);
  D_Flip_Flop d_ff_2 (.clk(d_ff_1_q), .D(in_1), .Q(d_ff_2_q), .en(and_1_out));  // open: Qn, preset, reset
  D_Flip_Flop d_ff_3 (.clk(d_ff_2_q), .D(in_1), .Q(d_ff_3_q), .en(and_1_out));  // open: Qn, preset, reset
  D_Flip_Flop d_ff_4 (.clk(d_ff_3_q), .D(in_1), .Q(out_2), .en(and_1_out));  // open: Qn, preset, reset

  // Notes on the sheet:
  //   Roll No.: 5
  //   Asynchronous counter that counts prime number from 0-15
  //   Name: Ashwin Maharjan
  //   Question No.: 8 (g) (i)
endmodule
