// Logisim project 8g(ii).circ as structural Verilog: 1 circuit, main circuit main
module main (
  output out_1,
  output out_2,
  output out_3,
  output out_4
);

  wire and_1_out, and_2_out, and_3_out, and_4_out, and_5_out, and_6_out, clock_1_out, not_1_out, not_2_out,
       not_3_out, not_4_out, not_5_out, not_6_out, not_7_out, or_1_out, or_2_out, or_3_out, or_4_out;

  and and_1 (and_1_out, out_2, out_3);
  and and_2 (and_2_out, out_3, out_1);
  not not_1 (not_1_out, out_1);
  not not_2 (not_2_out, out_3);
  not not_3 (not_3_out, out_2);
  not not_4 (not_4_out, out_3);
  not not_5 (not_5_out, out_4);
  not not_6 (not_6_out, out_4);
  not not_7 (not_7_out, out_3);
  and and_3 (and_3_out, not_1_out, out_2, not_2_out);
  and and_4 (and_4_out, not_3_out, out_3);
  and and_5 (and_5_out, out_3, out_1);
  or or_1 (or_1_out, not_4_out, out_2);
  or or_2 (or_2_out, and_1_out, and_2_out);
  or or_3 (or_3_out, not_6_out, not_7_out);
  or or_4 (or_4_out, and_3_out, and_4_out, and_5_out);
  and and_6 (and_6_out, or_1_out, not_5_out);
  Clock clock_1 (.out(clock_1_out));
  D_Flip_Flop d_ff_1 (.clk(clock_1_out), .D(or_2_out), .Q(out_4));  // open: Qn, preset, en, reset
  D_Flip_Flop d_ff_2 (.clk(clock_1_out), .D(or_4_out), .Q(out_3));  // open: Qn, preset, en, reset
  D_Flip_Flop d_ff_3 (.clk(clock_1_out), .D(and_6_out), .Q(out_2));  // open: Qn, preset, en, reset
  D_Flip_Flop d_ff_4 (.clk(clock_1_out), .D(or_3_out), .Q(out_1));  // open: Qn, preset, en, reset

  // Notes on the sheet:
  //   Synchronous counter that counts prime number from 0-15
  //   Name: Ashwin Maharjan
  //   Roll No.: 5
  //   Question No.: 8 (g) (ii)
endmodule
