// Logisim project 9c.circ as structural Verilog: 1 circuit, main circuit main
module main (
  input  in_1,
  input  in_2,
  input  in_3,
  output out_4,
  output out_5
);

  wire _1_out, _2_out, _3_out, _4_out, _5_out, _6_out, _7_out, _8_out, clock_1_out, d_ff_2_q, d_ff_3_q,
       not_1_out, or_1_out, or_2_out, or_3_out, or_4_out, undriven;

  Clock clock_1 (.out(clock_1_out));
  not not_1 (not_1_out, in_1);
  and _1 (_1_out, in_3, in_1);
  or or_1 (or_1_out, _1_out, _2_out);
  D_Flip_Flop d_ff_1 (.clk(clock_1_out), .D(or_1_out), .Q(out_5));  // open: Qn, preset, en, reset
  and _2 (_2_out, not_1_out, d_ff_2_q);
  and _3 (_3_out, out_5, in_1);
  or or_2 (or_2_out, _3_out, _4_out);
  D_Flip_Flop d_ff_2 (.clk(clock_1_out), .D(or_2_out), .Q(d_ff_2_q));  // open: Qn, preset, en, reset
  and _4 (_4_out, not_1_out, d_ff_3_q);
  and _5 (_5_out, d_ff_2_q, in_1);
  and _6 (_6_out, undriven, undriven, not_1_out, out_4);
  or or_3 (or_3_out, _5_out, _6_out);
  D_Flip_Flop d_ff_3 (.clk(clock_1_out), .D(or_3_out), .Q(d_ff_3_q));  // open: Qn, preset, en, reset
  and _7 (_7_out, d_ff_3_q, in_1);
  and _8 (_8_out, not_1_out, in_2);
  or or_4 (or_4_out, _7_out, _8_out);
  D_Flip_Flop d_ff_4 (.clk(clock_1_out), .D(or_4_out), .Q(out_4));  // open: Qn, preset, en, reset

  // Notes on the sheet:
  //   Roll No.: 5
  //   Question No.: 9 (c)
  //   Name: Ashwin Maharjan
endmodule
