// Logisim project 9d(i).circ as structural Verilog: 1 circuit, main circuit main
module main (
  input  in_1
);

  wire clock_1_out, d_ff_1_q, d_ff_2_q, d_ff_3_q, d_ff_4_q, d_ff_5_q;

  Clock clock_1 (.out(clock_1_out));
  D_Flip_Flop d_ff_1 (.clk(clock_1_out), .D(d_ff_5_q), .Q(d_ff_1_q), .preset(in_1), .reset(in_1));  // open: Qn, en
  D_Flip_Flop d_ff_2 (.clk(clock_1_out), .D(d_ff_1_q), .Q(d_ff_2_q), .reset(in_1));  // open: Qn, preset, en
  D_Flip_Flop d_ff_3 (.clk(clock_1_out), .D(d_ff_2_q), .Q(d_ff_3_q), .reset(in_1));  // open: Qn, preset, en
  D_Flip_Flop d_ff_4 (.clk(clock_1_out), .D(d_ff_3_q), .Q(d_ff_4_q), .reset(in_1));  // open: Qn, preset, en
  D_Flip_Flop d_ff_5 (.clk(clock_1_out), .D(d_ff_4_q), .Q(d_ff_5_q), .reset(in_1));  // open: Qn, preset, en

  // Notes on the sheet:
  //   Ring Counter
  //   Name: Ashwin Maharjan
  //   Roll No.: 5
  //   Question No.: 9 (d)(i)
endmodule
